// Logisim project best_SOC.circ as structural Verilog: 2 circuits, main circuit main
module main (
);

  wire undriven;
  wire [15:0] cpucore_1_addrout;
  wire [31:0] cpucore_1_dataout, ram_1_dout;

  RAM #(.addrWidth(16), .dataWidth(32), .enables("line")) ram_1 (
    .addr(cpucore_1_addrout), .clk(undriven), .din(cpucore_1_dataout), .dout(ram_1_dout));  // open: we
  CPUCore cpucore_1 (
    .DataIn(ram_1_dout), .DataOut(cpucore_1_dataout), .AddrOut(cpucore_1_addrout));  // open: Clock, Reset
endmodule

// A
module CPUCore (
  input  [31:0] DataIn,
  input  Clock,
  input  Reset,
  output [31:0] DataOut,
  output [15:0] AddrOut
);

  wire and_2_out, and_3_out, not_2_out, t_ff_1_q, t_ff_1_qn, xor_2_out;
  wire [7:0] pla_1_out, pla_2_out, pla_3_out;
  wire [31:0] A_q, adder_1_out, adder_2_out, and_1_out, B_q, C_q, controlled_buffer_2_out,
       controlled_buffer_3_out, controlled_buffer_12_out, controlled_buffer_13_out, D_q, E_q, F_q, G_q, H_q,
       IP_q, IR_q, not_1_out, or_1_out, shifter_1_out, shifter_2_out, subtractor_1_out, xor_1_out;
  wire [31:16] controlled_buffer_1_out;

  T_Flip_Flop t_ff_1 (.T(Clock), .clk(Clock), .Q(t_ff_1_q), .Qn(t_ff_1_qn), .reset(Reset));  // open: preset
  Register #(.width(32)) IP (.D(adder_1_out), .en(t_ff_1_q), .clk(t_ff_1_q), .Q(IP_q), .clr(Reset));
  PLA #(.in_width(3), .out_width(8), .\table ("000 00000001\n001 00000010\n010 00000100\n011 00001000\n100 00010000\n101 00100000\n110 01000000\n111 10000000")) pla_1 (
    .in(IR_q[21:19]), .out(pla_1_out));
  Register #(.width(32)) IR (.D(DataIn), .en(t_ff_1_q), .clk(t_ff_1_q), .Q(IR_q), .clr(Reset));
  assign {controlled_buffer_1_out, AddrOut} = t_ff_1_q ? IP_q : 32'bz;  // Controlled_Buffer controlled_buffer_1
  Adder #(.width(32)) adder_1 (.a(IP_q), .b(32'h1), .out(adder_1_out));  // open: cin, cout
  assign controlled_buffer_2_out = IR_q[0] ? DataIn : 32'bz;  // Controlled_Buffer controlled_buffer_2
  assign controlled_buffer_3_out = pla_1_out[0] ? adder_2_out : 32'bz;  // Controlled_Buffer controlled_buffer_3
  assign controlled_buffer_3_out = pla_1_out[1] ? subtractor_1_out : 32'bz;  // Controlled_Buffer controlled_buffer_4
  assign controlled_buffer_3_out = pla_1_out[2] ? and_1_out : 32'bz;  // Controlled_Buffer controlled_buffer_5
  assign and_1_out = controlled_buffer_13_out & controlled_buffer_12_out;  // AND_Gate and_1, 32 bits wide
  assign controlled_buffer_3_out = pla_1_out[3] ? or_1_out : 32'bz;  // Controlled_Buffer controlled_buffer_6
  assign or_1_out = controlled_buffer_13_out | controlled_buffer_12_out;  // OR_Gate or_1, 32 bits wide
  assign controlled_buffer_3_out = pla_1_out[4] ? xor_1_out : 32'bz;  // Controlled_Buffer controlled_buffer_7
  assign xor_1_out = controlled_buffer_13_out ^ controlled_buffer_12_out;  // XOR_Gate xor_1, 32 bits wide
  assign controlled_buffer_3_out = pla_1_out[5] ? not_1_out : 32'bz;  // Controlled_Buffer controlled_buffer_8
  assign not_1_out = ~controlled_buffer_13_out;  // NOT_Gate not_1, 32 bits wide
  assign controlled_buffer_3_out = pla_1_out[6] ? shifter_1_out : 32'bz;  // Controlled_Buffer controlled_buffer_9
  assign controlled_buffer_3_out = pla_1_out[7] ? shifter_2_out : 32'bz;  // Controlled_Buffer controlled_buffer_10
  Register #(.width(32)) A (.D(controlled_buffer_2_out), .en(IR_q[2]), .clk(Clock), .Q(A_q), .clr(Reset));
  assign controlled_buffer_2_out = IR_q[1] ? controlled_buffer_3_out : 32'bz;  // Controlled_Buffer controlled_buffer_11
  Register #(.width(32)) B (.D(controlled_buffer_2_out), .en(IR_q[3]), .clk(Clock), .Q(B_q), .clr(Reset));
  Register #(.width(32)) C (.D(controlled_buffer_2_out), .en(IR_q[4]), .clk(Clock), .Q(C_q), .clr(Reset));
  Register #(.width(32)) D (.D(controlled_buffer_2_out), .en(IR_q[5]), .clk(Clock), .Q(D_q), .clr(Reset));
  PLA #(.in_width(3), .out_width(8), .\table ("000 00000001\n001 00000010\n010 00000100\n011 00001000\n100 00010000\n101 00100000\n110 01000000\n111 10000000")) pla_2 (
    .in(IR_q[15:13]), .out(pla_2_out));
  PLA #(.in_width(3), .out_width(8), .\table ("000 00000001\n001 00000010\n010 00000100\n011 00001000\n100 00010000\n101 00100000\n110 01000000\n111 10000000")) pla_3 (
    .in(IR_q[18:16]), .out(pla_3_out));
  assign controlled_buffer_12_out = pla_3_out[0] ? A_q : 32'bz;  // Controlled_Buffer controlled_buffer_12
  assign controlled_buffer_13_out = pla_2_out[0] ? A_q : 32'bz;  // Controlled_Buffer controlled_buffer_13
  assign controlled_buffer_12_out = pla_3_out[1] ? B_q : 32'bz;  // Controlled_Buffer controlled_buffer_14
  assign controlled_buffer_13_out = pla_2_out[1] ? B_q : 32'bz;  // Controlled_Buffer controlled_buffer_15
  assign controlled_buffer_12_out = pla_3_out[2] ? C_q : 32'bz;  // Controlled_Buffer controlled_buffer_16
  assign controlled_buffer_13_out = pla_2_out[2] ? C_q : 32'bz;  // Controlled_Buffer controlled_buffer_17
  assign controlled_buffer_12_out = pla_3_out[3] ? D_q : 32'bz;  // Controlled_Buffer controlled_buffer_18
  assign controlled_buffer_13_out = pla_2_out[3] ? D_q : 32'bz;  // Controlled_Buffer controlled_buffer_19
  Subtractor #(.width(32)) subtractor_1 (
    .a(controlled_buffer_13_out), .b(controlled_buffer_12_out), .out(subtractor_1_out));  // open: bin, bout
  Adder #(.width(32)) adder_2 (
    .a(controlled_buffer_13_out), .b(controlled_buffer_12_out), .out(adder_2_out));  // open: cin, cout
  Shifter #(.width(32)) shifter_1 (
    .in(controlled_buffer_13_out), .\dist (controlled_buffer_12_out[4:0]), .out(shifter_1_out));
  Shifter #(.shift("rr"), .width(32)) shifter_2 (
    .in(controlled_buffer_13_out), .\dist (controlled_buffer_12_out[4:0]), .out(shifter_2_out));
  Register #(.width(32)) E (.D(controlled_buffer_2_out), .en(IR_q[6]), .clk(Clock), .Q(E_q), .clr(Reset));
  Register #(.width(32)) F (.D(controlled_buffer_2_out), .en(IR_q[7]), .clk(Clock), .Q(F_q), .clr(Reset));
  Register #(.width(32)) G (.D(controlled_buffer_2_out), .en(IR_q[8]), .clk(Clock), .Q(G_q), .clr(Reset));
  Register #(.width(32)) H (.D(controlled_buffer_2_out), .en(IR_q[9]), .clk(Clock), .Q(H_q), .clr(Reset));
  assign controlled_buffer_12_out = pla_3_out[4] ? E_q : 32'bz;  // Controlled_Buffer controlled_buffer_20
  assign controlled_buffer_13_out = pla_2_out[4] ? E_q : 32'bz;  // Controlled_Buffer controlled_buffer_21
  Controlled_Buffer #(.width(32)) controlled_buffer_22 (.in(F_q), .en(pla_3_out[5]));  // open: out
  assign controlled_buffer_13_out = pla_2_out[5] ? F_q : 32'bz;  // Controlled_Buffer controlled_buffer_23
  Controlled_Buffer #(.width(32)) controlled_buffer_24 (.in(G_q), .en(pla_3_out[6]));  // open: out
  assign controlled_buffer_13_out = pla_2_out[6] ? G_q : 32'bz;  // Controlled_Buffer controlled_buffer_25
  assign controlled_buffer_12_out = pla_3_out[7] ? H_q : 32'bz;  // Controlled_Buffer controlled_buffer_26
  assign controlled_buffer_13_out = pla_2_out[7] ? H_q : 32'bz;  // Controlled_Buffer controlled_buffer_27
  assign DataOut = IR_q[11] ? controlled_buffer_13_out : 32'bz;  // Controlled_Buffer controlled_buffer_28
  assign DataOut = IR_q[10] ? controlled_buffer_12_out : 32'bz;  // Controlled_Buffer controlled_buffer_29
  xor xor_2 (xor_2_out, IR_q[10], IR_q[11]);
  assign DataOut = not_2_out ? {32{1'b0}} : 32'bz;  // Controlled_Buffer controlled_buffer_30
  assign {controlled_buffer_1_out, AddrOut} = and_2_out ? controlled_buffer_13_out : 32'bz;  // Controlled_Buffer controlled_buffer_31
  assign {controlled_buffer_1_out, AddrOut} = and_3_out ? {32{1'b0}} : 32'bz;  // Controlled_Buffer controlled_buffer_32
  not not_2 (not_2_out, xor_2_out);
  and and_2 (and_2_out, IR_q[12], t_ff_1_qn);
  and and_3 (and_3_out, ~IR_q[12], t_ff_1_qn);  // AND_Gate
endmodule
